# Fritzing sketch ESP01_DHT22_NodeMCU (saved by Fritzing 0.9.2b)
stripboards: 1

parts:
  Input_3_5V = screw terminal, 3 pins
  J03 = female pin header, 2 pins [form="♀ (female)"]
  J04 = female pin header, 2 pins [form="♀ (female)"]
  DHT22 = Humidity and Temperature Sensor RHT03
  J01 = female pin header, 2 pins [form="♀ (female)"]
  J02 = female pin header, 2 pins [form="♀ (female)"]  # not connected
  U1 = ESP8266 WiFi Module [part_number=ESP8266]  # not connected

nets:
  N1: Input_3_5V.pin1, J04.pin1, DHT22.GND_2
  N2: Input_3_5V.pin3, J03.pin2, DHT22.Vcc, J01.pin2
  N3: J03.pin1, DHT22.Data-signal

notes:
  Connect ESP-01 to Pin Header with this orientation

custom parts:
  ESP8266 WiFi Module: Generic WiFi Module based on the ESP8266 with onboard PCB antenna and UART communications
