# Fritzing sketch ESP01_DHT22_NodeMCU_BB (saved by Fritzing 0.9.2b)
breadboards: 1

parts:
  DHT22 = Humidity and Temperature Sensor RHT03
  U2 = ESP8266 WiFi Module [part_number=ESP8266]
  Part2 = FTDI Basic Programmer

nets:
  VCC: DHT22.Vcc, U2.VCC, U2.CH_PD, Part2.POWER
  N1: DHT22.Data-signal, U2.GPIO_2
  N2: DHT22.GND_2, U2.GND, Part2.DTR
  N3: U2.RXD, Part2.TXO
  N4: U2.TXD, Part2.RXI

custom parts:
  ESP8266 WiFi Module: Generic WiFi Module based on the ESP8266 with onboard PCB antenna and UART communications
