# Fritzing sketch BathroomTempHum (saved by Fritzing 0.9.2b)
stripboards: 1

parts:
  RHT1 = Humidity and Temperature Sensor RHT03  # not connected
  J7 = female pin header, 2 pins [form="♀ (female)"]
  J6 = female pin header, 2 pins [form="♀ (female)"]
  J5 = female pin header, 2 pins [form="♀ (female)"]
  NRF24L1 = NRF24L01
  C1 = Electrolytic Capacitor [capacitance=4.7mF package="1010 [SMD, electrolytic]"]
  J19 = female pin header, 2 pins [form="♀ (female)"]
  J20 = female pin header, 12 pins [form="♀ (female)"]
  J21 = female pin header, 12 pins [form="♀ (female)"]
  Part2 = Arduino Pro Mini v13  # not connected
  J22 = male pin header, 4 pins [form="♂ (male)"]
  R3 = Resistor [tolerance=±5% resistance=1M package=THT]
  R4 = Resistor [tolerance=±10% resistance=470 package=THT]

nets:
  N1: J7.pin1, J20.pin9
  N2: J7.pin2, J20.pin11
  N3: J6.pin1, C1.+, J21.pin12
  N4: J6.pin2, J20.pin12
  N5: J5.pin1, J21.pin4
  N6: J5.pin2, C1.-, J20.pin4, J22.pin1
  N7: NRF24L1.MOSI, NRF24L1.IRQ
  N8: J19.pin1, J20.pin10
  N9: J19.pin2, J21.pin5
  N10: J20.pin1, R3.Pin_0
  N11: J20.pin2, J22.pin4, R4.Pin_0
  N12: J20.pin8, R3.Pin_1, R4.Pin_1
  N13: J21.pin6, J22.pin2

custom parts:
  NRF24L01: NRF24L01 module
