# Fritzing sketch GarageNodeV3 (saved by Fritzing 0.9.2b)
stripboards: 1

parts:
  Garage_door_-_Open = Pushbutton [package=THT]
  J6 = female pin header, 2 pins [form="♀ (female)"]
  J7 = female pin header, 2 pins [form="♀ (female)"]
  RHT1 = Humidity and Temperature Sensor RHT03
  J5 = female pin header, 2 pins [form="♀ (female)"]
  J18 = screw terminal, 3 pins
  Garage_door_-_Closed = Pushbutton [package=THT]
  NRF24L1 = NRF24L01  # not connected
  J8 = female pin header, 2 pins [form="♀ (female)"]
  Nano1 = Arduino Nano v2.3
  U1 = TLP621 [package=THT]
  U2 = TLP621 [package=THT]
  DIP-Relay1 = DIP-Relay-D31A [part_number=D31A*]
  J1 = screw terminal, 3 pins
  J19 = screw terminal, 3 pins
  R1 = Resistor [tolerance=±5% resistance=220 package="0805 [SMD]"]
  R2 = Resistor [tolerance=±5% resistance=220 package="0805 [SMD]"]
  J20 = screw terminal, 3 pins
  J11 = double row male pin header, 4 pins [form="♂ (male)"]
  C2 = Electrolytic Capacitor [capacitance=4.7mF package="1010 [SMD, electrolytic]"]
  M1 = DC Motor  # not connected

nets:
  N1: Garage_door_-_Open.leg0, U2.Pin_2, J19.pin3
  N2: Garage_door_-_Open.leg1, RHT1.GND_2, Garage_door_-_Closed.leg1, J8.pin2, Nano1.GND, U1.Pin_4, U2.Pin_3, DIP-Relay1.COIL1_+, J1.pin3, J20.pin1, J11.pin4, C2.-
  N3: J6.pin1, Nano1.D11
  N4: J6.pin2, Nano1.D13
  N5: J7.pin1, Nano1.D10
  N6: J7.pin2, Nano1.D9
  VCC: RHT1.Vcc, J8.pin1, Nano1.3V3, J11.pin2, C2.+
  N7: RHT1.Data-signal, Nano1.D6, J11.pin3
  N8: J5.pin1, Nano1.D2
  N9: J5.pin2, Nano1.D12
  N10: J18.pin1, DIP-Relay1.B2_Switch_Terminal_B
  N11: J18.pin3, DIP-Relay1.A2_Switch_Terminal_A
  N12: Garage_door_-_Closed.leg0, U1.Pin_2, J19.pin1
  N13: Nano1.D3, U1.Pin_3
  N14: Nano1.D4, U2.Pin_4
  N15: Nano1.D7, DIP-Relay1.Coil2_-
  N16: Nano1.+5V, J1.pin1, R1.Pin_0, R2.Pin_1
  N17: U1.Pin_1, R1.Pin_1
  N18: U2.Pin_1, R2.Pin_0

notes:
  Trigger Garage door motor.

custom parts:
  NRF24L01: NRF24L01 module
