# Fritzing sketch MySensorsTemp (saved by Fritzing 0.9.2b)
stripboards: 1

parts:
  RHT1 = Humidity and Temperature Sensor RHT03
  J18 = screw terminal, 3 pins  # not connected
  J7 = female pin header, 2 pins [form="♀ (female)"]  # not connected
  J6 = female pin header, 2 pins [form="♀ (female)"]  # not connected
  J5 = female pin header, 2 pins [form="♀ (female)"]
  NRF24L1 = NRF24L01
  C1 = Electrolytic Capacitor [capacitance=4.7mF package="1010 [SMD, electrolytic]"]
  J19 = female pin header, 2 pins [form="♀ (female)"]  # not connected
  Part1 = Arduino Pro Mini v13  # not connected
  R1 = Resistor [tolerance=±5% resistance=470 package=THT]
  R2 = Resistor [tolerance=±5% resistance=1M package=THT]

nets:
  N1: RHT1.Vcc, J5.pin2, C1.+, R2.Pin_0
  N2: RHT1.GND_2, R1.Pin_0
  N3: J5.pin1, C1.-
  N4: NRF24L1.MOSI, NRF24L1.IRQ
  N5: R1.Pin_1, R2.Pin_1

custom parts:
  NRF24L01: NRF24L01 module
